// Logisim project DisplayControll.circ as structural Verilog: 3 circuits, main circuit main
module main (
  input  in_1
);

  wire button_1_out, clock_1_out, clock_2_out, displaydriver_1_collision, pull_resistor_1_node;
  wire [1:0] displaydriver_1_collidersaved;
  wire [3:0] adder_1_out;
  wire [7:0] counter_1_q, multiplexer_1_out, rom_1_data;
  wire [7:4] adder_1_out_2;
  wire [15:0] displaydriver_1_out_6, displaydriver_1_out_7, displaydriver_1_out_8, displaydriver_1_out_9,
       displaydriver_1_out_10, displaydriver_1_out_11, displaydriver_1_out_12, displaydriver_1_out_13,
       displaydriver_1_out_14, displaydriver_1_out_15, displaydriver_1_out_16, displaydriver_1_out_17,
       displaydriver_1_out_18, displaydriver_1_out_19, displaydriver_1_out_20, displaydriver_1_out_21;

  Multiplexer #(.width(8)) multiplexer_1 (
    .in0({adder_1_out_2, adder_1_out}), .in1({8{1'b0}}), .out(multiplexer_1_out), .sel(in_1));  // open: en
  Clock #(.highDuration(2), .lowDuration(2)) clock_1 (.out(clock_1_out));
  ROM rom_1 (.addr({adder_1_out_2, adder_1_out}), .data(rom_1_data));  // open: sel
  // Probe on {adder_1_out_2, adder_1_out}
  // Probe on adder_1_out
  Counter counter_1 (.D(multiplexer_1_out), .Q(counter_1_q), .clk(clock_1_out));  // open: load, count, carry, clr
  // Probe on rom_1_data
  Adder adder_1 (.a({8{1'b0}}), .b(counter_1_q), .out({adder_1_out_2, adder_1_out}));  // open: cin, cout
  Button button_1 (.out(button_1_out));
  displayDriver displaydriver_1 (
    .data(rom_1_data), .mem_slot({adder_1_out_2, adder_1_out}), .out_6(displaydriver_1_out_6),
    .out_7(displaydriver_1_out_7), .out_8(displaydriver_1_out_8), .out_9(displaydriver_1_out_9),
    .out_10(displaydriver_1_out_10), .out_11(displaydriver_1_out_11), .out_12(displaydriver_1_out_12),
    .out_13(displaydriver_1_out_13), .out_14(displaydriver_1_out_14), .out_15(displaydriver_1_out_15),
    .out_16(displaydriver_1_out_16), .out_17(displaydriver_1_out_17), .out_18(displaydriver_1_out_18),
    .out_19(displaydriver_1_out_19), .out_20(displaydriver_1_out_20), .out_21(displaydriver_1_out_21),
    .CLK(clock_2_out), .shutdown(pull_resistor_1_node), .RESET(button_1_out),
    .collision(displaydriver_1_collision), .colliderSaved(displaydriver_1_collidersaved));  // open: colliderRT
  Pull_Resistor pull_resistor_1 (.node(pull_resistor_1_node));
  Clock clock_2 (.out(clock_2_out));
  // Probe on displaydriver_1_collision
  // Probe on displaydriver_1_collidersaved
  DotMatrix #(.inputtype("row"), .matrixcols(16), .matrixrows(16)) dotmatrix_1 (
    .row0(displaydriver_1_out_6), .row1(displaydriver_1_out_7), .row2(displaydriver_1_out_8),
    .row3(displaydriver_1_out_9), .row4(displaydriver_1_out_10), .row5(displaydriver_1_out_11),
    .row6(displaydriver_1_out_12), .row7(displaydriver_1_out_13), .row8(displaydriver_1_out_14),
    .row9(displaydriver_1_out_15), .row10(displaydriver_1_out_16), .row11(displaydriver_1_out_17),
    .row12(displaydriver_1_out_18), .row13(displaydriver_1_out_19), .row14(displaydriver_1_out_20),
    .row15(displaydriver_1_out_21));

  // Notes on the sheet:
  //   contents of rom_1 (hex, n*v repeats v):
  //   1 1 0 0 1 1 0 0 1 1 0 0 1 1 0 1 1 14*0 1 1 14*0 1 1 6*0 1 1 6*0 1 1 5*0 1 0 0 1 5*0 1 1 5*0 1 0 0 1
  //   5*0 1 1 5*0 1 0 0 1 5*0 1 1 5*0 1 0 0 1 5*0 1 1 4*0 1 1 0 0 1 1 4*0 1 1 0 0 0 1 0 0 1 1 0 0 1 0 0 0
  //   1 1 0 0 0 1 0 0 1 1 0 0 1 0 0 0 1 1 4*0 1 1 0 0 1 1 4*0 1 1 14*0 1 1 14*0 1 1 0 1 0 1 0 1 0 1 0 1 0
  //   1 0 18*1
endmodule

module _16bitDispCntrl (
  input  shutdown,
  input  clk,
  input  [7:0] DATA,
  input  [7:0] mem_slot,
  input  RESET,
  output [1:0] collider,
  output collision,
  output [15:0] result
);

  wire comparator_1_eq, comparator_2_eq, comparator_3_eq, comparator_4_eq, comparator_5_eq, comparator_6_eq,
       comparator_7_eq, comparator_8_eq, comparator_9_eq, comparator_10_eq, comparator_11_eq,
       comparator_12_eq, comparator_13_eq, comparator_14_eq, comparator_15_eq, comparator_16_eq,
       pull_resistor_1_node, r1, r2, r3, r4, r5, r6, r7, r8, r9, r10, r11, r12, r13, r14, r15, r16;
  wire [1:0] collider_t;
  wire [1:1] register_1_q, register_2_q, register_3_q, register_4_q, register_5_q, register_6_q,
       register_7_q, register_8_q, register_9_q, register_10_q, register_11_q, register_12_q, register_13_q,
       register_14_q, register_15_q, register_16_q;

  Pull_Resistor pull_resistor_1 (.node(pull_resistor_1_node));
  Transistor #(.\type ("n")) transistor_1 (.in(clk), .out(pull_resistor_1_node), .gate(shutdown));
  Comparator #(.width(4), .mode("unsigned")) comparator_1 (
    .a(mem_slot[3:0]), .b(4'b0000), .eq(comparator_1_eq));  // open: gt, lt
  Comparator #(.width(4), .mode("unsigned")) comparator_2 (
    .a(mem_slot[3:0]), .b(4'b0001), .eq(comparator_2_eq));  // open: gt, lt
  Comparator #(.width(4), .mode("unsigned")) comparator_3 (
    .a(mem_slot[3:0]), .b(4'b0010), .eq(comparator_3_eq));  // open: gt, lt
  Comparator #(.width(4), .mode("unsigned")) comparator_4 (
    .a(mem_slot[3:0]), .b(4'b0011), .eq(comparator_4_eq));  // open: gt, lt
  Comparator #(.width(4), .mode("unsigned")) comparator_5 (
    .a(mem_slot[3:0]), .b(4'b0100), .eq(comparator_5_eq));  // open: gt, lt
  Comparator #(.width(4), .mode("unsigned")) comparator_6 (
    .a(mem_slot[3:0]), .b(4'b0101), .eq(comparator_6_eq));  // open: gt, lt
  Comparator #(.width(4), .mode("unsigned")) comparator_7 (
    .a(mem_slot[3:0]), .b(4'b0110), .eq(comparator_7_eq));  // open: gt, lt
  Comparator #(.width(4), .mode("unsigned")) comparator_8 (
    .a(mem_slot[3:0]), .b(4'b0111), .eq(comparator_8_eq));  // open: gt, lt
  Comparator #(.width(4), .mode("unsigned")) comparator_9 (
    .a(mem_slot[3:0]), .b(4'b1000), .eq(comparator_9_eq));  // open: gt, lt
  Comparator #(.width(4), .mode("unsigned")) comparator_10 (
    .a(mem_slot[3:0]), .b(4'b1001), .eq(comparator_10_eq));  // open: gt, lt
  Comparator #(.width(4), .mode("unsigned")) comparator_11 (
    .a(mem_slot[3:0]), .b(4'b1010), .eq(comparator_11_eq));  // open: gt, lt
  Comparator #(.width(4), .mode("unsigned")) comparator_12 (
    .a(mem_slot[3:0]), .b(4'b1011), .eq(comparator_12_eq));  // open: gt, lt
  Comparator #(.width(4), .mode("unsigned")) comparator_13 (
    .a(mem_slot[3:0]), .b(4'b1100), .eq(comparator_13_eq));  // open: gt, lt
  Comparator #(.width(4), .mode("unsigned")) comparator_14 (
    .a(mem_slot[3:0]), .b(4'b1101), .eq(comparator_14_eq));  // open: gt, lt
  Comparator #(.width(4), .mode("unsigned")) comparator_15 (
    .a(mem_slot[3:0]), .b(4'b1110), .eq(comparator_15_eq));  // open: gt, lt
  Comparator #(.width(4), .mode("unsigned")) comparator_16 (
    .a(mem_slot[3:0]), .b(4'b1111), .eq(comparator_16_eq));  // open: gt, lt
  and and_1 (r1, DATA[0], comparator_1_eq, pull_resistor_1_node, result[15]);
  and and_2 (r2, DATA[0], comparator_2_eq, pull_resistor_1_node, result[14]);
  and and_3 (r3, DATA[0], comparator_3_eq, pull_resistor_1_node, result[13]);
  and and_4 (r4, DATA[0], comparator_4_eq, pull_resistor_1_node, result[12]);
  and and_5 (r5, DATA[0], comparator_5_eq, pull_resistor_1_node, result[11]);
  and and_6 (r6, DATA[0], comparator_6_eq, pull_resistor_1_node, result[10]);
  and and_7 (r7, DATA[0], comparator_7_eq, pull_resistor_1_node, result[9]);
  and and_8 (r8, DATA[0], comparator_8_eq, pull_resistor_1_node, result[8]);
  and and_9 (r9, DATA[0], comparator_9_eq, pull_resistor_1_node, result[7]);
  and and_10 (r10, DATA[0], comparator_10_eq, pull_resistor_1_node, result[6]);
  and and_11 (r11, DATA[0], comparator_11_eq, pull_resistor_1_node, result[5]);
  and and_12 (r12, DATA[0], comparator_12_eq, pull_resistor_1_node, result[4]);
  and and_13 (r13, DATA[0], comparator_13_eq, pull_resistor_1_node, result[3]);
  and and_14 (r14, DATA[0], comparator_14_eq, pull_resistor_1_node, result[2]);
  and and_15 (r15, DATA[0], comparator_15_eq, pull_resistor_1_node, result[1]);
  and and_16 (r16, DATA[0], comparator_16_eq, pull_resistor_1_node, result[0]);
  or or_1 (collision, r1, r2, r3, r4, r5, r6, r7, r8, r9, r10, r11, r12, r13, r14, r15, r16);
  Register #(.width(2), .trigger("falling")) register_1 (
    .D(DATA[1:0]), .en(comparator_1_eq), .Q({register_1_q[1], result[15]}), .clk(pull_resistor_1_node),
    .clr(RESET));
  Register #(.width(2), .trigger("falling")) register_2 (
    .D(DATA[1:0]), .en(comparator_2_eq), .Q({register_2_q[1], result[14]}), .clk(pull_resistor_1_node),
    .clr(RESET));
  Register #(.width(2), .trigger("falling")) register_3 (
    .D(DATA[1:0]), .en(comparator_3_eq), .Q({register_3_q[1], result[13]}), .clk(pull_resistor_1_node),
    .clr(RESET));
  Register #(.width(2), .trigger("falling")) register_4 (
    .D(DATA[1:0]), .en(comparator_4_eq), .Q({register_4_q[1], result[12]}), .clk(pull_resistor_1_node),
    .clr(RESET));
  Register #(.width(2), .trigger("falling")) register_5 (
    .D(DATA[1:0]), .en(comparator_5_eq), .Q({register_5_q[1], result[11]}), .clk(pull_resistor_1_node),
    .clr(RESET));
  Register #(.width(2), .trigger("falling")) register_6 (
    .D(DATA[1:0]), .en(comparator_6_eq), .Q({register_6_q[1], result[10]}), .clk(pull_resistor_1_node),
    .clr(RESET));
  Register #(.width(2), .trigger("falling")) register_7 (
    .D(DATA[1:0]), .en(comparator_7_eq), .Q({register_7_q[1], result[9]}), .clk(pull_resistor_1_node),
    .clr(RESET));
  Register #(.width(2), .trigger("falling")) register_8 (
    .D(DATA[1:0]), .en(comparator_8_eq), .Q({register_8_q[1], result[8]}), .clk(pull_resistor_1_node),
    .clr(RESET));
  Register #(.width(2), .trigger("falling")) register_9 (
    .D(DATA[1:0]), .en(comparator_9_eq), .Q({register_9_q[1], result[7]}), .clk(pull_resistor_1_node),
    .clr(RESET));
  Register #(.width(2), .trigger("falling")) register_10 (
    .D(DATA[1:0]), .en(comparator_10_eq), .Q({register_10_q[1], result[6]}), .clk(pull_resistor_1_node),
    .clr(RESET));
  Register #(.width(2), .trigger("falling")) register_11 (
    .D(DATA[1:0]), .en(comparator_11_eq), .Q({register_11_q[1], result[5]}), .clk(pull_resistor_1_node),
    .clr(RESET));
  Register #(.width(2), .trigger("falling")) register_12 (
    .D(DATA[1:0]), .en(comparator_12_eq), .Q({register_12_q[1], result[4]}), .clk(pull_resistor_1_node),
    .clr(RESET));
  Register #(.width(2), .trigger("falling")) register_13 (
    .D(DATA[1:0]), .en(comparator_13_eq), .Q({register_13_q[1], result[3]}), .clk(pull_resistor_1_node),
    .clr(RESET));
  Register #(.width(2), .trigger("falling")) register_14 (
    .D(DATA[1:0]), .en(comparator_14_eq), .Q({register_14_q[1], result[2]}), .clk(pull_resistor_1_node),
    .clr(RESET));
  Register #(.width(2), .trigger("falling")) register_15 (
    .D(DATA[1:0]), .en(comparator_15_eq), .Q({register_15_q[1], result[1]}), .clk(pull_resistor_1_node),
    .clr(RESET));
  Register #(.width(2), .trigger("falling")) register_16 (
    .D(DATA[1:0]), .en(comparator_16_eq), .Q({register_16_q[1], result[0]}), .clk(pull_resistor_1_node),
    .clr(RESET));
  Transistor #(.\type ("n"), .width(2)) transistor_2 (
    .in({register_1_q[1], result[15]}), .out(collider_t), .gate(comparator_1_eq));
  Transistor #(.\type ("n"), .width(2)) transistor_3 (
    .in({register_2_q[1], result[14]}), .out(collider_t), .gate(comparator_2_eq));
  Transistor #(.\type ("n"), .width(2)) transistor_4 (
    .in({register_3_q[1], result[13]}), .out(collider_t), .gate(comparator_3_eq));
  Transistor #(.\type ("n"), .width(2)) transistor_5 (
    .in({register_4_q[1], result[12]}), .out(collider_t), .gate(comparator_4_eq));
  Transistor #(.\type ("n"), .width(2)) transistor_6 (
    .in({register_5_q[1], result[11]}), .out(collider_t), .gate(comparator_5_eq));
  Transistor #(.\type ("n"), .width(2)) transistor_7 (
    .in({register_6_q[1], result[10]}), .out(collider_t), .gate(comparator_6_eq));
  Transistor #(.\type ("n"), .width(2)) transistor_8 (
    .in({register_7_q[1], result[9]}), .out(collider_t), .gate(comparator_7_eq));
  Transistor #(.\type ("n"), .width(2)) transistor_9 (
    .in({register_8_q[1], result[8]}), .out(collider_t), .gate(comparator_8_eq));
  Transistor #(.\type ("n"), .width(2)) transistor_10 (
    .in({register_9_q[1], result[7]}), .out(collider_t), .gate(comparator_9_eq));
  Transistor #(.\type ("n"), .width(2)) transistor_11 (
    .in({register_10_q[1], result[6]}), .out(collider_t), .gate(comparator_10_eq));
  Transistor #(.\type ("n"), .width(2)) transistor_12 (
    .in({register_11_q[1], result[5]}), .out(collider_t), .gate(comparator_11_eq));
  Transistor #(.\type ("n"), .width(2)) transistor_13 (
    .in({register_12_q[1], result[4]}), .out(collider_t), .gate(comparator_12_eq));
  Transistor #(.\type ("n"), .width(2)) transistor_14 (
    .in({register_13_q[1], result[3]}), .out(collider_t), .gate(comparator_13_eq));
  Transistor #(.\type ("n"), .width(2)) transistor_15 (
    .in({register_14_q[1], result[2]}), .out(collider_t), .gate(comparator_14_eq));
  Transistor #(.\type ("n"), .width(2)) transistor_16 (
    .in({register_15_q[1], result[1]}), .out(collider_t), .gate(comparator_15_eq));
  Transistor #(.\type ("n"), .width(2)) transistor_17 (
    .in({register_16_q[1], result[0]}), .out(collider_t), .gate(comparator_16_eq));
  Transistor #(.\type ("n"), .width(2)) transistor_18 (.in(collider_t), .out(collider), .gate(collision));
  Pull_Resistor pull_resistor_2 (.node(collider));

  // Other names for the same wires on the sheet: o16 = result[0]; o15 = result[1]; o14 = result[2]; o13 = result[3];
  //   o12 = result[4]; o11 = result[5]; o10 = result[6]; o9 = result[7]; o8 = result[8]; o7 = result[9];
  //   o6 = result[10]; o5 = result[11]; o4 = result[12]; o3 = result[13]; o2 = result[14]; o1 = result[15]
endmodule

module displayDriver (
  input  [7:0] data,
  input  [7:0] mem_slot,
  input  CLK,
  input  shutdown,
  input  RESET,
  output [15:0] out_6,
  output [15:0] out_7,
  output [15:0] out_8,
  output [15:0] out_9,
  output [15:0] out_10,
  output [15:0] out_11,
  output [15:0] out_12,
  output [15:0] out_13,
  output [15:0] out_14,
  output [15:0] out_15,
  output [15:0] out_16,
  output [15:0] out_17,
  output [15:0] out_18,
  output [15:0] out_19,
  output [15:0] out_20,
  output [15:0] out_21,
  output collision,
  output [1:0] colliderSaved,
  output [1:0] colliderRT
);

  wire clk_t, comparator_1_eq, comparator_2_eq, comparator_3_eq, comparator_4_eq, comparator_5_eq,
       comparator_6_eq, comparator_7_eq, comparator_8_eq, comparator_9_eq, comparator_10_eq,
       comparator_11_eq, comparator_12_eq, comparator_13_eq, comparator_14_eq, comparator_15_eq,
       comparator_16_eq, r1, r2, r3, r4, r5, r6, r7, r8, r9, r10, r11, r12, r13, r14, r15, r16;
  wire [1:0] n16bitdispcntrl_1_collider, n16bitdispcntrl_2_collider, n16bitdispcntrl_3_collider,
       n16bitdispcntrl_4_collider, n16bitdispcntrl_5_collider, n16bitdispcntrl_6_collider,
       n16bitdispcntrl_7_collider, n16bitdispcntrl_8_collider, n16bitdispcntrl_9_collider,
       n16bitdispcntrl_10_collider, n16bitdispcntrl_11_collider, n16bitdispcntrl_12_collider,
       n16bitdispcntrl_13_collider, n16bitdispcntrl_14_collider, n16bitdispcntrl_15_collider,
       n16bitdispcntrl_16_collider;

  Transistor #(.gate("br")) transistor_1 (.in(CLK), .out(clk_t), .gate(shutdown));
  Pull_Resistor pull_resistor_1 (.node(clk_t));
  Comparator #(.width(4), .mode("unsigned")) comparator_1 (
    .a(mem_slot[7:4]), .b(4'b0000), .eq(comparator_1_eq));  // open: gt, lt
  Comparator #(.width(4), .mode("unsigned")) comparator_2 (
    .a(mem_slot[7:4]), .b(4'b0001), .eq(comparator_2_eq));  // open: gt, lt
  Comparator #(.width(4), .mode("unsigned")) comparator_3 (
    .a(mem_slot[7:4]), .b(4'b0010), .eq(comparator_3_eq));  // open: gt, lt
  Comparator #(.width(4), .mode("unsigned")) comparator_4 (
    .a(mem_slot[7:4]), .b(4'b0011), .eq(comparator_4_eq));  // open: gt, lt
  Comparator #(.width(4), .mode("unsigned")) comparator_5 (
    .a(mem_slot[7:4]), .b(4'b0100), .eq(comparator_5_eq));  // open: gt, lt
  Comparator #(.width(4), .mode("unsigned")) comparator_6 (
    .a(mem_slot[7:4]), .b(4'b0101), .eq(comparator_6_eq));  // open: gt, lt
  Comparator #(.width(4), .mode("unsigned")) comparator_7 (
    .a(mem_slot[7:4]), .b(4'b0110), .eq(comparator_7_eq));  // open: gt, lt
  Comparator #(.width(4), .mode("unsigned")) comparator_8 (
    .a(mem_slot[7:4]), .b(4'b0111), .eq(comparator_8_eq));  // open: gt, lt
  _16bitDispCntrl u_16bitdispcntrl_1 (
    .DATA(data), .mem_slot(mem_slot), .clk(clk_t), .result(out_6), .shutdown(comparator_1_eq),
    .collision(r1), .collider(n16bitdispcntrl_1_collider), .RESET(RESET));
  _16bitDispCntrl u_16bitdispcntrl_2 (
    .DATA(data), .mem_slot(mem_slot), .clk(clk_t), .result(out_7), .shutdown(comparator_2_eq),
    .collision(r2), .collider(n16bitdispcntrl_2_collider), .RESET(RESET));
  _16bitDispCntrl u_16bitdispcntrl_3 (
    .DATA(data), .mem_slot(mem_slot), .clk(clk_t), .result(out_8), .shutdown(comparator_3_eq),
    .collision(r3), .collider(n16bitdispcntrl_3_collider), .RESET(RESET));
  _16bitDispCntrl u_16bitdispcntrl_4 (
    .DATA(data), .mem_slot(mem_slot), .clk(clk_t), .result(out_9), .shutdown(comparator_4_eq),
    .collision(r4), .collider(n16bitdispcntrl_4_collider), .RESET(RESET));
  _16bitDispCntrl u_16bitdispcntrl_5 (
    .DATA(data), .mem_slot(mem_slot), .clk(clk_t), .result(out_10), .shutdown(comparator_5_eq),
    .collision(r5), .collider(n16bitdispcntrl_5_collider), .RESET(RESET));
  _16bitDispCntrl u_16bitdispcntrl_6 (
    .DATA(data), .mem_slot(mem_slot), .clk(clk_t), .result(out_11), .shutdown(comparator_6_eq),
    .collision(r6), .collider(n16bitdispcntrl_6_collider), .RESET(RESET));
  _16bitDispCntrl u_16bitdispcntrl_7 (
    .DATA(data), .mem_slot(mem_slot), .clk(clk_t), .result(out_12), .shutdown(comparator_7_eq),
    .collision(r7), .collider(n16bitdispcntrl_7_collider), .RESET(RESET));
  _16bitDispCntrl u_16bitdispcntrl_8 (
    .DATA(data), .mem_slot(mem_slot), .clk(clk_t), .result(out_13), .shutdown(comparator_8_eq),
    .collision(r8), .collider(n16bitdispcntrl_8_collider), .RESET(RESET));
  Transistor #(.\type ("n"), .width(2)) transistor_2 (
    .in(n16bitdispcntrl_1_collider), .out(colliderRT), .gate(comparator_1_eq));
  Transistor #(.\type ("n"), .width(2)) transistor_3 (
    .in(n16bitdispcntrl_2_collider), .out(colliderRT), .gate(comparator_2_eq));
  Transistor #(.\type ("n"), .width(2)) transistor_4 (
    .in(n16bitdispcntrl_3_collider), .out(colliderRT), .gate(comparator_3_eq));
  Transistor #(.\type ("n"), .width(2)) transistor_5 (
    .in(n16bitdispcntrl_4_collider), .out(colliderRT), .gate(comparator_4_eq));
  Transistor #(.\type ("n"), .width(2)) transistor_6 (
    .in(n16bitdispcntrl_5_collider), .out(colliderRT), .gate(comparator_5_eq));
  Transistor #(.\type ("n"), .width(2)) transistor_7 (
    .in(n16bitdispcntrl_6_collider), .out(colliderRT), .gate(comparator_6_eq));
  Transistor #(.\type ("n"), .width(2)) transistor_8 (
    .in(n16bitdispcntrl_7_collider), .out(colliderRT), .gate(comparator_7_eq));
  Transistor #(.\type ("n"), .width(2)) transistor_9 (
    .in(n16bitdispcntrl_8_collider), .out(colliderRT), .gate(comparator_8_eq));
  Comparator #(.width(4), .mode("unsigned")) comparator_9 (
    .a(mem_slot[7:4]), .b(4'b1000), .eq(comparator_9_eq));  // open: gt, lt
  Comparator #(.width(4), .mode("unsigned")) comparator_10 (
    .a(mem_slot[7:4]), .b(4'b1001), .eq(comparator_10_eq));  // open: gt, lt
  Comparator #(.width(4), .mode("unsigned")) comparator_11 (
    .a(mem_slot[7:4]), .b(4'b1010), .eq(comparator_11_eq));  // open: gt, lt
  Comparator #(.width(4), .mode("unsigned")) comparator_12 (
    .a(mem_slot[7:4]), .b(4'b1011), .eq(comparator_12_eq));  // open: gt, lt
  Comparator #(.width(4), .mode("unsigned")) comparator_13 (
    .a(mem_slot[7:4]), .b(4'b1100), .eq(comparator_13_eq));  // open: gt, lt
  Comparator #(.width(4), .mode("unsigned")) comparator_14 (
    .a(mem_slot[7:4]), .b(4'b1101), .eq(comparator_14_eq));  // open: gt, lt
  Comparator #(.width(4), .mode("unsigned")) comparator_15 (
    .a(mem_slot[7:4]), .b(4'b1110), .eq(comparator_15_eq));  // open: gt, lt
  Comparator #(.width(4), .mode("unsigned")) comparator_16 (
    .a(mem_slot[7:4]), .b(4'b1111), .eq(comparator_16_eq));  // open: gt, lt
  _16bitDispCntrl u_16bitdispcntrl_9 (
    .DATA(data), .mem_slot(mem_slot), .clk(clk_t), .result(out_14), .shutdown(comparator_9_eq),
    .collision(r9), .collider(n16bitdispcntrl_9_collider), .RESET(RESET));
  _16bitDispCntrl u_16bitdispcntrl_10 (
    .DATA(data), .mem_slot(mem_slot), .clk(clk_t), .result(out_15), .shutdown(comparator_10_eq),
    .collision(r10), .collider(n16bitdispcntrl_10_collider), .RESET(RESET));
  _16bitDispCntrl u_16bitdispcntrl_11 (
    .DATA(data), .mem_slot(mem_slot), .clk(clk_t), .result(out_16), .shutdown(comparator_11_eq),
    .collision(r11), .collider(n16bitdispcntrl_11_collider), .RESET(RESET));
  _16bitDispCntrl u_16bitdispcntrl_12 (
    .DATA(data), .mem_slot(mem_slot), .clk(clk_t), .result(out_17), .shutdown(comparator_12_eq),
    .collision(r12), .collider(n16bitdispcntrl_12_collider), .RESET(RESET));
  _16bitDispCntrl u_16bitdispcntrl_13 (
    .DATA(data), .mem_slot(mem_slot), .clk(clk_t), .result(out_18), .shutdown(comparator_13_eq),
    .collision(r13), .collider(n16bitdispcntrl_13_collider), .RESET(RESET));
  _16bitDispCntrl u_16bitdispcntrl_14 (
    .DATA(data), .mem_slot(mem_slot), .clk(clk_t), .result(out_19), .shutdown(comparator_14_eq),
    .collision(r14), .collider(n16bitdispcntrl_14_collider), .RESET(RESET));
  _16bitDispCntrl u_16bitdispcntrl_15 (
    .DATA(data), .mem_slot(mem_slot), .clk(clk_t), .result(out_20), .shutdown(comparator_15_eq),
    .collision(r15), .collider(n16bitdispcntrl_15_collider), .RESET(RESET));
  _16bitDispCntrl u_16bitdispcntrl_16 (
    .DATA(data), .mem_slot(mem_slot), .clk(clk_t), .result(out_21), .shutdown(comparator_16_eq),
    .collision(r16), .collider(n16bitdispcntrl_16_collider), .RESET(RESET));
  Transistor #(.\type ("n"), .width(2)) transistor_10 (
    .in(n16bitdispcntrl_9_collider), .out(colliderRT), .gate(comparator_9_eq));
  Transistor #(.\type ("n"), .width(2)) transistor_11 (
    .in(n16bitdispcntrl_10_collider), .out(colliderRT), .gate(comparator_10_eq));
  Transistor #(.\type ("n"), .width(2)) transistor_12 (
    .in(n16bitdispcntrl_11_collider), .out(colliderRT), .gate(comparator_11_eq));
  Transistor #(.\type ("n"), .width(2)) transistor_13 (
    .in(n16bitdispcntrl_12_collider), .out(colliderRT), .gate(comparator_12_eq));
  Transistor #(.\type ("n"), .width(2)) transistor_14 (
    .in(n16bitdispcntrl_13_collider), .out(colliderRT), .gate(comparator_13_eq));
  Transistor #(.\type ("n"), .width(2)) transistor_15 (
    .in(n16bitdispcntrl_14_collider), .out(colliderRT), .gate(comparator_14_eq));
  Transistor #(.\type ("n"), .width(2)) transistor_16 (
    .in(n16bitdispcntrl_15_collider), .out(colliderRT), .gate(comparator_15_eq));
  Transistor #(.\type ("n"), .width(2)) transistor_17 (
    .in(n16bitdispcntrl_16_collider), .out(colliderRT), .gate(comparator_16_eq));
  // Probe on colliderRT
  or or_1 (collision, r1, r2, r3, r4, r5, r6, r7, r8, r9, r10, r11, r12, r13, r14, r15, r16);
  // Probe on colliderSaved
  Register #(.width(2), .trigger("high")) register_1 (
    .D(colliderRT), .en(collision), .Q(colliderSaved), .clk(clk_t), .clr(RESET));

  // Other names for the same wires on the sheet: collider[1:0] = colliderRT
endmodule
