// Logisim project test.circ as structural Verilog: 5 circuits, main circuit main
module main (
  input  in_1
);

  wire button_1_out, clk, clock_2_out, clock_3_out;
  wire [3:0] adder_1_out;
  wire [7:0] cdm_8_1_pc, cdm_8_1_r0, cdm_8_1_r1, cdm_8_1_r2, cdm_8_1_r3, cdm_8_1_sp, counter_1_q,
       multiplexer_1_out, rom_1_data;
  wire [7:4] adder_1_out_2;
  wire [15:0] displaydriver_fullframeupdate_1_out_4, displaydriver_fullframeupdate_1_out_5,
       displaydriver_fullframeupdate_1_out_6, displaydriver_fullframeupdate_1_out_7,
       displaydriver_fullframeupdate_1_out_8, displaydriver_fullframeupdate_1_out_9,
       displaydriver_fullframeupdate_1_out_10, displaydriver_fullframeupdate_1_out_11,
       displaydriver_fullframeupdate_1_out_12, displaydriver_fullframeupdate_1_out_13,
       displaydriver_fullframeupdate_1_out_14, displaydriver_fullframeupdate_1_out_15,
       displaydriver_fullframeupdate_1_out_16, displaydriver_fullframeupdate_1_out_17,
       displaydriver_fullframeupdate_1_out_18, displaydriver_fullframeupdate_1_out_19;

  // Probe on cdm_8_1_r0
  Clock clock_1 (.out(clk));
  // Probe on cdm_8_1_r3
  // Probe on cdm_8_1_r1
  // Probe on cdm_8_1_r2
  Button button_1 (.out(button_1_out));
  // Probe on cdm_8_1_sp
  // Probe on cdm_8_1_pc
  CdM_8 cdm_8_1 (
    .R0(cdm_8_1_r0), .R1(cdm_8_1_r1), .R2(cdm_8_1_r2), .R3(cdm_8_1_r3), .PC(cdm_8_1_pc), .SP(cdm_8_1_sp),
    .clk(clk), .rset(button_1_out));  // open: data_code_prime, mem, load_st_prime, addr, data_out, data_in, page, PS, IAck, IRQ, vector, shadow
  Multiplexer #(.width(8)) multiplexer_1 (
    .in0({adder_1_out_2, adder_1_out}), .in1({8{1'b0}}), .out(multiplexer_1_out), .sel(in_1));  // open: en
  Clock #(.highDuration(2), .lowDuration(2)) clock_2 (.out(clock_2_out));
  ROM rom_1 (.addr({adder_1_out_2, adder_1_out}), .data(rom_1_data));  // open: sel
  // Probe on {adder_1_out_2, adder_1_out}
  // Probe on adder_1_out
  Counter counter_1 (.D(multiplexer_1_out), .Q(counter_1_q), .clk(clock_2_out));  // open: load, count, carry, clr
  // Probe on rom_1_data
  Adder adder_1 (.a({8{1'b0}}), .b(counter_1_q), .out({adder_1_out_2, adder_1_out}));  // open: cin, cout
  displayDriver_fullFrameUpdate displaydriver_fullframeupdate_1 (
    .data(rom_1_data), .mem_slot({adder_1_out_2, adder_1_out}),
    .out_4(displaydriver_fullframeupdate_1_out_4), .out_5(displaydriver_fullframeupdate_1_out_5),
    .out_6(displaydriver_fullframeupdate_1_out_6), .out_7(displaydriver_fullframeupdate_1_out_7),
    .out_8(displaydriver_fullframeupdate_1_out_8), .out_9(displaydriver_fullframeupdate_1_out_9),
    .out_10(displaydriver_fullframeupdate_1_out_10), .out_11(displaydriver_fullframeupdate_1_out_11),
    .out_12(displaydriver_fullframeupdate_1_out_12), .out_13(displaydriver_fullframeupdate_1_out_13),
    .out_14(displaydriver_fullframeupdate_1_out_14), .out_15(displaydriver_fullframeupdate_1_out_15),
    .out_16(displaydriver_fullframeupdate_1_out_16), .out_17(displaydriver_fullframeupdate_1_out_17),
    .out_18(displaydriver_fullframeupdate_1_out_18), .out_19(displaydriver_fullframeupdate_1_out_19),
    .CLK(clock_3_out));
  Clock clock_3 (.out(clock_3_out));
  DotMatrix #(.inputtype("row"), .matrixcols(16), .matrixrows(16), .persist(1024)) dotmatrix_1 (
    .row0(displaydriver_fullframeupdate_1_out_4), .row1(displaydriver_fullframeupdate_1_out_5),
    .row2(displaydriver_fullframeupdate_1_out_6), .row3(displaydriver_fullframeupdate_1_out_7),
    .row4(displaydriver_fullframeupdate_1_out_8), .row5(displaydriver_fullframeupdate_1_out_9),
    .row6(displaydriver_fullframeupdate_1_out_10), .row7(displaydriver_fullframeupdate_1_out_11),
    .row8(displaydriver_fullframeupdate_1_out_12), .row9(displaydriver_fullframeupdate_1_out_13),
    .row10(displaydriver_fullframeupdate_1_out_14), .row11(displaydriver_fullframeupdate_1_out_15),
    .row12(displaydriver_fullframeupdate_1_out_16), .row13(displaydriver_fullframeupdate_1_out_17),
    .row14(displaydriver_fullframeupdate_1_out_18), .row15(displaydriver_fullframeupdate_1_out_19));
  // Probe on displaydriver_fullframeupdate_1_out_4
  // Probe on displaydriver_fullframeupdate_1_out_5
  // Probe on displaydriver_fullframeupdate_1_out_6
  // Probe on displaydriver_fullframeupdate_1_out_7
  // Probe on displaydriver_fullframeupdate_1_out_8
  // Probe on displaydriver_fullframeupdate_1_out_9
  // Probe on displaydriver_fullframeupdate_1_out_10
  // Probe on displaydriver_fullframeupdate_1_out_11
  // Probe on displaydriver_fullframeupdate_1_out_12
  // Probe on displaydriver_fullframeupdate_1_out_13
  // Probe on displaydriver_fullframeupdate_1_out_14
  // Probe on displaydriver_fullframeupdate_1_out_15
  // Probe on displaydriver_fullframeupdate_1_out_16
  // Probe on displaydriver_fullframeupdate_1_out_17
  // Probe on displaydriver_fullframeupdate_1_out_18
  // Probe on displaydriver_fullframeupdate_1_out_19

  // Notes on the sheet:
  //   contents of rom_1 (hex, n*v repeats v):
  //   1 1 0 0 1 1 0 0 1 1 0 0 1 1 0 1 1 14*0 1 1 14*0 1 1 6*0 1 1 6*0 1 1 5*0 1 0 0 1 5*0 1 1 5*0 1 0 0 1
  //   5*0 1 1 5*0 1 0 0 1 5*0 1 1 5*0 1 0 0 1 5*0 1 1 4*0 1 1 0 0 1 1 4*0 1 1 0 0 0 1 0 0 1 1 0 0 1 0 0 0
  //   1 1 0 0 0 1 0 0 1 1 0 0 1 0 0 0 1 1 4*0 1 1 0 0 1 1 4*0 1 1 14*0 1 1 14*0 1 1 14*0 17*1
endmodule

module _16bitDispCntrl (
  input  shutdown,
  input  clk,
  input  [7:0] DATA,
  input  [7:0] mem_slot,
  output [15:0] result
);

  wire pull_resistor_1_node, pull_resistor_2_node;

  Pull_Resistor pull_resistor_1 (.node(pull_resistor_1_node));
  Transistor transistor_1 (.in(clk), .out(pull_resistor_1_node), .gate(shutdown));
  Pull_Resistor pull_resistor_2 (.node(pull_resistor_2_node));
  Transistor #(.\type ("n")) transistor_2 (.in(DATA[0]), .out(pull_resistor_2_node), .gate(pull_resistor_1_node));
  _4bitComparator_1 u_4bitcomparator_1_1 (
    .in_2(mem_slot[3:0]), .out_3(result[15]), .out_4(result[14]), .out_5(result[13]), .out_6(result[12]),
    .out_7(result[11]), .out_8(result[10]), .out_9(result[9]), .out_10(result[8]), .out_11(result[7]),
    .out_12(result[6]), .out_13(result[5]), .out_14(result[4]), .out_15(result[3]), .out_16(result[2]),
    .out_17(result[1]), .out_18(result[0]), .in_1(pull_resistor_2_node));
endmodule

module displayDriver_fullFrameUpdate (
  input  [7:0] data,
  input  [7:0] mem_slot,
  input  CLK,
  output [15:0] out_4,
  output [15:0] out_5,
  output [15:0] out_6,
  output [15:0] out_7,
  output [15:0] out_8,
  output [15:0] out_9,
  output [15:0] out_10,
  output [15:0] out_11,
  output [15:0] out_12,
  output [15:0] out_13,
  output [15:0] out_14,
  output [15:0] out_15,
  output [15:0] out_16,
  output [15:0] out_17,
  output [15:0] out_18,
  output [15:0] out_19
);

  wire pull_resistor_1_node;
  wire [15:0] n16bitdispcntrl_1_result;

  _16bitDispCntrl u_16bitdispcntrl_1 (
    .DATA(data), .mem_slot(mem_slot), .clk(CLK), .result(n16bitdispcntrl_1_result),
    .shutdown(pull_resistor_1_node));
  Pull_Resistor pull_resistor_1 (.node(pull_resistor_1_node));
  _4bitComparator_16 u_4bitcomparator_16_1 (
    .in_2(mem_slot[7:4]), .out_3(out_4), .out_4(out_5), .out_5(out_6), .out_6(out_7), .out_7(out_8),
    .out_8(out_9), .out_9(out_10), .out_10(out_11), .out_11(out_12), .out_12(out_13), .out_13(out_14),
    .out_14(out_15), .out_15(out_16), .out_16(out_17), .out_17(out_18), .out_18(out_19),
    .in_1(n16bitdispcntrl_1_result));
endmodule

module _4bitComparator_1 (
  input  in_1,
  input  [3:0] in_2,
  output out_3,
  output out_4,
  output out_5,
  output out_6,
  output out_7,
  output out_8,
  output out_9,
  output out_10,
  output out_11,
  output out_12,
  output out_13,
  output out_14,
  output out_15,
  output out_16,
  output out_17,
  output out_18
);

  wire comparator_1_eq, comparator_2_eq, comparator_3_eq, comparator_4_eq, comparator_5_eq, comparator_6_eq,
       comparator_7_eq, comparator_8_eq, comparator_9_eq, comparator_10_eq, comparator_11_eq,
       comparator_12_eq, comparator_13_eq, comparator_14_eq, comparator_15_eq, comparator_16_eq;

  Comparator #(.width(4), .mode("unsigned")) comparator_1 (
    .a(in_2), .b(4'b0000), .eq(comparator_1_eq));  // open: gt, lt
  Comparator #(.width(4), .mode("unsigned")) comparator_2 (
    .a(in_2), .b(4'b0001), .eq(comparator_2_eq));  // open: gt, lt
  Comparator #(.width(4), .mode("unsigned")) comparator_3 (
    .a(in_2), .b(4'b0010), .eq(comparator_3_eq));  // open: gt, lt
  Comparator #(.width(4), .mode("unsigned")) comparator_4 (
    .a(in_2), .b(4'b0011), .eq(comparator_4_eq));  // open: gt, lt
  Comparator #(.width(4), .mode("unsigned")) comparator_5 (
    .a(in_2), .b(4'b0100), .eq(comparator_5_eq));  // open: gt, lt
  Comparator #(.width(4), .mode("unsigned")) comparator_6 (
    .a(in_2), .b(4'b0101), .eq(comparator_6_eq));  // open: gt, lt
  Comparator #(.width(4), .mode("unsigned")) comparator_7 (
    .a(in_2), .b(4'b0110), .eq(comparator_7_eq));  // open: gt, lt
  Comparator #(.width(4), .mode("unsigned")) comparator_8 (
    .a(in_2), .b(4'b0111), .eq(comparator_8_eq));  // open: gt, lt
  Comparator #(.width(4), .mode("unsigned")) comparator_9 (
    .a(in_2), .b(4'b1000), .eq(comparator_9_eq));  // open: gt, lt
  Comparator #(.width(4), .mode("unsigned")) comparator_10 (
    .a(in_2), .b(4'b1001), .eq(comparator_10_eq));  // open: gt, lt
  Comparator #(.width(4), .mode("unsigned")) comparator_11 (
    .a(in_2), .b(4'b1010), .eq(comparator_11_eq));  // open: gt, lt
  Comparator #(.width(4), .mode("unsigned")) comparator_12 (
    .a(in_2), .b(4'b1011), .eq(comparator_12_eq));  // open: gt, lt
  Comparator #(.width(4), .mode("unsigned")) comparator_13 (
    .a(in_2), .b(4'b1100), .eq(comparator_13_eq));  // open: gt, lt
  Comparator #(.width(4), .mode("unsigned")) comparator_14 (
    .a(in_2), .b(4'b1101), .eq(comparator_14_eq));  // open: gt, lt
  Comparator #(.width(4), .mode("unsigned")) comparator_15 (
    .a(in_2), .b(4'b1110), .eq(comparator_15_eq));  // open: gt, lt
  Comparator #(.width(4), .mode("unsigned")) comparator_16 (
    .a(in_2), .b(4'b1111), .eq(comparator_16_eq));  // open: gt, lt
  Transistor #(.\type ("n")) transistor_1 (.in(in_1), .out(out_3), .gate(comparator_1_eq));
  Transistor #(.\type ("n")) transistor_2 (.in(in_1), .out(out_4), .gate(comparator_2_eq));
  Transistor #(.\type ("n")) transistor_3 (.in(in_1), .out(out_5), .gate(comparator_3_eq));
  Transistor #(.\type ("n")) transistor_4 (.in(in_1), .out(out_6), .gate(comparator_4_eq));
  Transistor #(.\type ("n")) transistor_5 (.in(in_1), .out(out_7), .gate(comparator_5_eq));
  Transistor #(.\type ("n")) transistor_6 (.in(in_1), .out(out_8), .gate(comparator_6_eq));
  Transistor #(.\type ("n")) transistor_7 (.in(in_1), .out(out_9), .gate(comparator_7_eq));
  Transistor #(.\type ("n")) transistor_8 (.in(in_1), .out(out_10), .gate(comparator_8_eq));
  Transistor #(.\type ("n")) transistor_9 (.in(in_1), .out(out_11), .gate(comparator_9_eq));
  Transistor #(.\type ("n")) transistor_10 (.in(in_1), .out(out_12), .gate(comparator_10_eq));
  Transistor #(.\type ("n")) transistor_11 (.in(in_1), .out(out_13), .gate(comparator_11_eq));
  Transistor #(.\type ("n")) transistor_12 (.in(in_1), .out(out_14), .gate(comparator_12_eq));
  Transistor #(.\type ("n")) transistor_13 (.in(in_1), .out(out_15), .gate(comparator_13_eq));
  Transistor #(.\type ("n")) transistor_14 (.in(in_1), .out(out_16), .gate(comparator_14_eq));
  Transistor #(.\type ("n")) transistor_15 (.in(in_1), .out(out_17), .gate(comparator_15_eq));
  Transistor #(.\type ("n")) transistor_16 (.in(in_1), .out(out_18), .gate(comparator_16_eq));
  Pull_Resistor pull_resistor_1 (.node(out_3));
  Pull_Resistor pull_resistor_2 (.node(out_4));
  Pull_Resistor pull_resistor_3 (.node(out_5));
  Pull_Resistor pull_resistor_4 (.node(out_6));
  Pull_Resistor pull_resistor_5 (.node(out_7));
  Pull_Resistor pull_resistor_6 (.node(out_8));
  Pull_Resistor pull_resistor_7 (.node(out_9));
  Pull_Resistor pull_resistor_8 (.node(out_10));
  Pull_Resistor pull_resistor_9 (.node(out_11));
  Pull_Resistor pull_resistor_10 (.node(out_12));
  Pull_Resistor pull_resistor_11 (.node(out_13));
  Pull_Resistor pull_resistor_12 (.node(out_14));
  Pull_Resistor pull_resistor_13 (.node(out_15));
  Pull_Resistor pull_resistor_14 (.node(out_16));
  Pull_Resistor pull_resistor_15 (.node(out_17));
  Pull_Resistor pull_resistor_16 (.node(out_18));
endmodule

module _4bitComparator_16 (
  input  [15:0] in_1,
  input  [3:0] in_2,
  output [15:0] out_3,
  output [15:0] out_4,
  output [15:0] out_5,
  output [15:0] out_6,
  output [15:0] out_7,
  output [15:0] out_8,
  output [15:0] out_9,
  output [15:0] out_10,
  output [15:0] out_11,
  output [15:0] out_12,
  output [15:0] out_13,
  output [15:0] out_14,
  output [15:0] out_15,
  output [15:0] out_16,
  output [15:0] out_17,
  output [15:0] out_18
);

  wire comparator_1_eq, comparator_2_eq, comparator_3_eq, comparator_4_eq, comparator_5_eq, comparator_6_eq,
       comparator_7_eq, comparator_8_eq, comparator_9_eq, comparator_10_eq, comparator_11_eq,
       comparator_12_eq, comparator_13_eq, comparator_14_eq, comparator_15_eq, comparator_16_eq;

  Comparator #(.width(4), .mode("unsigned")) comparator_1 (
    .a(in_2), .b(4'b0000), .eq(comparator_1_eq));  // open: gt, lt
  Comparator #(.width(4), .mode("unsigned")) comparator_2 (
    .a(in_2), .b(4'b0001), .eq(comparator_2_eq));  // open: gt, lt
  Comparator #(.width(4), .mode("unsigned")) comparator_3 (
    .a(in_2), .b(4'b0010), .eq(comparator_3_eq));  // open: gt, lt
  Comparator #(.width(4), .mode("unsigned")) comparator_4 (
    .a(in_2), .b(4'b0011), .eq(comparator_4_eq));  // open: gt, lt
  Comparator #(.width(4), .mode("unsigned")) comparator_5 (
    .a(in_2), .b(4'b0100), .eq(comparator_5_eq));  // open: gt, lt
  Comparator #(.width(4), .mode("unsigned")) comparator_6 (
    .a(in_2), .b(4'b0101), .eq(comparator_6_eq));  // open: gt, lt
  Comparator #(.width(4), .mode("unsigned")) comparator_7 (
    .a(in_2), .b(4'b0110), .eq(comparator_7_eq));  // open: gt, lt
  Comparator #(.width(4), .mode("unsigned")) comparator_8 (
    .a(in_2), .b(4'b0111), .eq(comparator_8_eq));  // open: gt, lt
  Comparator #(.width(4), .mode("unsigned")) comparator_9 (
    .a(in_2), .b(4'b1000), .eq(comparator_9_eq));  // open: gt, lt
  Comparator #(.width(4), .mode("unsigned")) comparator_10 (
    .a(in_2), .b(4'b1001), .eq(comparator_10_eq));  // open: gt, lt
  Comparator #(.width(4), .mode("unsigned")) comparator_11 (
    .a(in_2), .b(4'b1010), .eq(comparator_11_eq));  // open: gt, lt
  Comparator #(.width(4), .mode("unsigned")) comparator_12 (
    .a(in_2), .b(4'b1011), .eq(comparator_12_eq));  // open: gt, lt
  Comparator #(.width(4), .mode("unsigned")) comparator_13 (
    .a(in_2), .b(4'b1100), .eq(comparator_13_eq));  // open: gt, lt
  Comparator #(.width(4), .mode("unsigned")) comparator_14 (
    .a(in_2), .b(4'b1101), .eq(comparator_14_eq));  // open: gt, lt
  Comparator #(.width(4), .mode("unsigned")) comparator_15 (
    .a(in_2), .b(4'b1110), .eq(comparator_15_eq));  // open: gt, lt
  Comparator #(.width(4), .mode("unsigned")) comparator_16 (
    .a(in_2), .b(4'b1111), .eq(comparator_16_eq));  // open: gt, lt
  Pull_Resistor pull_resistor_1 (.node(out_3));
  Transistor #(.\type ("n"), .width(16)) transistor_1 (.in(in_1), .out(out_3), .gate(comparator_1_eq));
  Pull_Resistor pull_resistor_2 (.node(out_4));
  Transistor #(.\type ("n"), .width(16)) transistor_2 (.in(in_1), .out(out_4), .gate(comparator_2_eq));
  Pull_Resistor pull_resistor_3 (.node(out_5));
  Transistor #(.\type ("n"), .width(16)) transistor_3 (.in(in_1), .out(out_5), .gate(comparator_3_eq));
  Pull_Resistor pull_resistor_4 (.node(out_6));
  Transistor #(.\type ("n"), .width(16)) transistor_4 (.in(in_1), .out(out_6), .gate(comparator_4_eq));
  Pull_Resistor pull_resistor_5 (.node(out_7));
  Transistor #(.\type ("n"), .width(16)) transistor_5 (.in(in_1), .out(out_7), .gate(comparator_5_eq));
  Pull_Resistor pull_resistor_6 (.node(out_8));
  Transistor #(.\type ("n"), .width(16)) transistor_6 (.in(in_1), .out(out_8), .gate(comparator_6_eq));
  Pull_Resistor pull_resistor_7 (.node(out_9));
  Transistor #(.\type ("n"), .width(16)) transistor_7 (.in(in_1), .out(out_9), .gate(comparator_7_eq));
  Pull_Resistor pull_resistor_8 (.node(out_10));
  Transistor #(.\type ("n"), .width(16)) transistor_8 (.in(in_1), .out(out_10), .gate(comparator_8_eq));
  Pull_Resistor pull_resistor_9 (.node(out_11));
  Transistor #(.\type ("n"), .width(16)) transistor_9 (.in(in_1), .out(out_11), .gate(comparator_9_eq));
  Pull_Resistor pull_resistor_10 (.node(out_12));
  Transistor #(.\type ("n"), .width(16)) transistor_10 (.in(in_1), .out(out_12), .gate(comparator_10_eq));
  Pull_Resistor pull_resistor_11 (.node(out_13));
  Transistor #(.\type ("n"), .width(16)) transistor_11 (.in(in_1), .out(out_13), .gate(comparator_11_eq));
  Pull_Resistor pull_resistor_12 (.node(out_14));
  Transistor #(.\type ("n"), .width(16)) transistor_12 (.in(in_1), .out(out_14), .gate(comparator_12_eq));
  Pull_Resistor pull_resistor_13 (.node(out_15));
  Transistor #(.\type ("n"), .width(16)) transistor_13 (.in(in_1), .out(out_15), .gate(comparator_13_eq));
  Pull_Resistor pull_resistor_14 (.node(out_16));
  Transistor #(.\type ("n"), .width(16)) transistor_14 (.in(in_1), .out(out_16), .gate(comparator_14_eq));
  Pull_Resistor pull_resistor_15 (.node(out_17));
  Transistor #(.\type ("n"), .width(16)) transistor_15 (.in(in_1), .out(out_17), .gate(comparator_15_eq));
  Pull_Resistor pull_resistor_16 (.node(out_18));
  Transistor #(.\type ("n"), .width(16)) transistor_16 (.in(in_1), .out(out_18), .gate(comparator_16_eq));
endmodule
