// Logisim project testold.circ as structural Verilog: 3 circuits, main circuit main
module main (
);

  wire clock_1_out;
  wire [15:0] displaydriver_1_out_5, displaydriver_1_out_6, displaydriver_1_out_7, displaydriver_1_out_8,
       displaydriver_1_out_9, displaydriver_1_out_10, displaydriver_1_out_11, displaydriver_1_out_12,
       displaydriver_1_out_13, displaydriver_1_out_14, displaydriver_1_out_15, displaydriver_1_out_16,
       displaydriver_1_out_17, displaydriver_1_out_18, displaydriver_1_out_19, displaydriver_1_out_20;

  displayDriver displaydriver_1 (
    .out_5(displaydriver_1_out_5), .out_6(displaydriver_1_out_6), .out_7(displaydriver_1_out_7),
    .out_8(displaydriver_1_out_8), .out_9(displaydriver_1_out_9), .out_10(displaydriver_1_out_10),
    .out_11(displaydriver_1_out_11), .out_12(displaydriver_1_out_12), .out_13(displaydriver_1_out_13),
    .out_14(displaydriver_1_out_14), .out_15(displaydriver_1_out_15), .out_16(displaydriver_1_out_16),
    .out_17(displaydriver_1_out_17), .out_18(displaydriver_1_out_18), .out_19(displaydriver_1_out_19),
    .out_20(displaydriver_1_out_20), .CLK(clock_1_out));  // open: data, mem_slot, shutdown
  Clock clock_1 (.out(clock_1_out));
  DotMatrix #(.inputtype("row"), .matrixcols(16), .matrixrows(16)) dotmatrix_1 (
    .row0(displaydriver_1_out_5), .row1(displaydriver_1_out_6), .row2(displaydriver_1_out_7),
    .row3(displaydriver_1_out_8), .row4(displaydriver_1_out_9), .row5(displaydriver_1_out_10),
    .row6(displaydriver_1_out_11), .row7(displaydriver_1_out_12), .row8(displaydriver_1_out_13),
    .row9(displaydriver_1_out_14), .row10(displaydriver_1_out_15), .row11(displaydriver_1_out_16),
    .row12(displaydriver_1_out_17), .row13(displaydriver_1_out_18), .row14(displaydriver_1_out_19),
    .row15(displaydriver_1_out_20));
endmodule

module _16bitDispCntrl (
  input  shutdown,
  input  clk,
  input  [7:0] DATA,
  input  [7:0] mem_slot,
  output [15:0] result
);

  wire comparator_1_eq, comparator_2_eq, comparator_3_eq, comparator_4_eq, comparator_5_eq, comparator_6_eq,
       comparator_7_eq, comparator_8_eq, comparator_9_eq, comparator_10_eq, comparator_11_eq,
       comparator_12_eq, comparator_13_eq, comparator_14_eq, comparator_15_eq, comparator_16_eq,
       transistor_1_out;

  Transistor #(.\type ("n")) transistor_1 (.in(clk), .out(transistor_1_out), .gate(shutdown));
  Pull_Resistor pull_resistor_1 (.node(transistor_1_out));
  Comparator #(.width(4), .mode("unsigned")) comparator_1 (
    .a(mem_slot[3:0]), .b(4'b0000), .eq(comparator_1_eq));  // open: gt, lt
  Comparator #(.width(4), .mode("unsigned")) comparator_2 (
    .a(mem_slot[3:0]), .b(4'b0001), .eq(comparator_2_eq));  // open: gt, lt
  Comparator #(.width(4), .mode("unsigned")) comparator_3 (
    .a(mem_slot[3:0]), .b(4'b0010), .eq(comparator_3_eq));  // open: gt, lt
  Comparator #(.width(4), .mode("unsigned")) comparator_4 (
    .a(mem_slot[3:0]), .b(4'b0011), .eq(comparator_4_eq));  // open: gt, lt
  Comparator #(.width(4), .mode("unsigned")) comparator_5 (
    .a(mem_slot[3:0]), .b(4'b0100), .eq(comparator_5_eq));  // open: gt, lt
  Comparator #(.width(4), .mode("unsigned")) comparator_6 (
    .a(mem_slot[3:0]), .b(4'b0101), .eq(comparator_6_eq));  // open: gt, lt
  Comparator #(.width(4), .mode("unsigned")) comparator_7 (
    .a(mem_slot[3:0]), .b(4'b0110), .eq(comparator_7_eq));  // open: gt, lt
  Comparator #(.width(4), .mode("unsigned")) comparator_8 (
    .a(mem_slot[3:0]), .b(4'b0111), .eq(comparator_8_eq));  // open: gt, lt
  Comparator #(.width(4), .mode("unsigned")) comparator_9 (
    .a(mem_slot[3:0]), .b(4'b1000), .eq(comparator_9_eq));  // open: gt, lt
  Comparator #(.width(4), .mode("unsigned")) comparator_10 (
    .a(mem_slot[3:0]), .b(4'b1001), .eq(comparator_10_eq));  // open: gt, lt
  Comparator #(.width(4), .mode("unsigned")) comparator_11 (
    .a(mem_slot[3:0]), .b(4'b1010), .eq(comparator_11_eq));  // open: gt, lt
  Comparator #(.width(4), .mode("unsigned")) comparator_12 (
    .a(mem_slot[3:0]), .b(4'b1011), .eq(comparator_12_eq));  // open: gt, lt
  Comparator #(.width(4), .mode("unsigned")) comparator_13 (
    .a(mem_slot[3:0]), .b(4'b1100), .eq(comparator_13_eq));  // open: gt, lt
  Comparator #(.width(4), .mode("unsigned")) comparator_14 (
    .a(mem_slot[3:0]), .b(4'b1101), .eq(comparator_14_eq));  // open: gt, lt
  Comparator #(.width(4), .mode("unsigned")) comparator_15 (
    .a(mem_slot[3:0]), .b(4'b1110), .eq(comparator_15_eq));  // open: gt, lt
  Comparator #(.width(4), .mode("unsigned")) comparator_16 (
    .a(mem_slot[3:0]), .b(4'b1111), .eq(comparator_16_eq));  // open: gt, lt
  Register #(.width(1)) register_1 (
    .D(DATA[0]), .en(comparator_1_eq), .Q(result[15]), .clk(transistor_1_out));  // open: clr
  Register #(.width(1)) register_2 (
    .D(DATA[0]), .en(comparator_2_eq), .Q(result[14]), .clk(transistor_1_out));  // open: clr
  Register #(.width(1)) register_3 (
    .D(DATA[0]), .en(comparator_3_eq), .Q(result[13]), .clk(transistor_1_out));  // open: clr
  Register #(.width(1)) register_4 (
    .D(DATA[0]), .en(comparator_4_eq), .Q(result[12]), .clk(transistor_1_out));  // open: clr
  Register #(.width(1)) register_5 (
    .D(DATA[0]), .en(comparator_5_eq), .Q(result[11]), .clk(transistor_1_out));  // open: clr
  Register #(.width(1)) register_6 (
    .D(DATA[0]), .en(comparator_6_eq), .Q(result[10]), .clk(transistor_1_out));  // open: clr
  Register #(.width(1)) register_7 (
    .D(DATA[0]), .en(comparator_7_eq), .Q(result[9]), .clk(transistor_1_out));  // open: clr
  Register #(.width(1)) register_8 (
    .D(DATA[0]), .en(comparator_8_eq), .Q(result[8]), .clk(transistor_1_out));  // open: clr
  Register #(.width(1)) register_9 (
    .D(DATA[0]), .en(comparator_9_eq), .Q(result[7]), .clk(transistor_1_out));  // open: clr
  Register #(.width(1)) register_10 (
    .D(DATA[0]), .en(comparator_10_eq), .Q(result[6]), .clk(transistor_1_out));  // open: clr
  Register #(.width(1)) register_11 (
    .D(DATA[0]), .en(comparator_11_eq), .Q(result[5]), .clk(transistor_1_out));  // open: clr
  Register #(.width(1)) register_12 (
    .D(DATA[0]), .en(comparator_12_eq), .Q(result[4]), .clk(transistor_1_out));  // open: clr
  Register #(.width(1)) register_13 (
    .D(DATA[0]), .en(comparator_13_eq), .Q(result[3]), .clk(transistor_1_out));  // open: clr
  Register #(.width(1)) register_14 (
    .D(DATA[0]), .en(comparator_14_eq), .Q(result[2]), .clk(transistor_1_out));  // open: clr
  Register #(.width(1)) register_15 (
    .D(DATA[0]), .en(comparator_15_eq), .Q(result[1]), .clk(transistor_1_out));  // open: clr
  Register #(.width(1)) register_16 (
    .D(DATA[0]), .en(comparator_16_eq), .Q(result[0]), .clk(transistor_1_out));  // open: clr
endmodule

module displayDriver (
  input  [7:0] data,
  input  [7:0] mem_slot,
  input  CLK,
  input  shutdown,
  output [15:0] out_5,
  output [15:0] out_6,
  output [15:0] out_7,
  output [15:0] out_8,
  output [15:0] out_9,
  output [15:0] out_10,
  output [15:0] out_11,
  output [15:0] out_12,
  output [15:0] out_13,
  output [15:0] out_14,
  output [15:0] out_15,
  output [15:0] out_16,
  output [15:0] out_17,
  output [15:0] out_18,
  output [15:0] out_19,
  output [15:0] out_20
);

  wire comparator_1_eq, comparator_2_eq, comparator_3_eq, comparator_4_eq, comparator_5_eq, comparator_6_eq,
       comparator_7_eq, comparator_8_eq, comparator_9_eq, comparator_10_eq, comparator_11_eq,
       comparator_12_eq, comparator_13_eq, comparator_14_eq, comparator_15_eq, comparator_16_eq,
       transistor_1_out;

  Transistor #(.gate("br")) transistor_1 (.in(CLK), .out(transistor_1_out), .gate(shutdown));
  Pull_Resistor pull_resistor_1 (.node(transistor_1_out));
  Comparator #(.width(4), .mode("unsigned")) comparator_1 (
    .a(mem_slot[7:4]), .b(4'b0000), .eq(comparator_1_eq));  // open: gt, lt
  Comparator #(.width(4), .mode("unsigned")) comparator_2 (
    .a(mem_slot[7:4]), .b(4'b0001), .eq(comparator_2_eq));  // open: gt, lt
  Comparator #(.width(4), .mode("unsigned")) comparator_3 (
    .a(mem_slot[7:4]), .b(4'b0010), .eq(comparator_3_eq));  // open: gt, lt
  Comparator #(.width(4), .mode("unsigned")) comparator_4 (
    .a(mem_slot[7:4]), .b(4'b0011), .eq(comparator_4_eq));  // open: gt, lt
  Comparator #(.width(4), .mode("unsigned")) comparator_5 (
    .a(mem_slot[7:4]), .b(4'b0100), .eq(comparator_5_eq));  // open: gt, lt
  Comparator #(.width(4), .mode("unsigned")) comparator_6 (
    .a(mem_slot[7:4]), .b(4'b0101), .eq(comparator_6_eq));  // open: gt, lt
  Comparator #(.width(4), .mode("unsigned")) comparator_7 (
    .a(mem_slot[7:4]), .b(4'b0110), .eq(comparator_7_eq));  // open: gt, lt
  Comparator #(.width(4), .mode("unsigned")) comparator_8 (
    .a(mem_slot[7:4]), .b(4'b0111), .eq(comparator_8_eq));  // open: gt, lt
  _16bitDispCntrl u_16bitdispcntrl_1 (
    .DATA(data), .mem_slot(mem_slot), .clk(transistor_1_out), .result(out_5), .shutdown(comparator_1_eq));
  _16bitDispCntrl u_16bitdispcntrl_2 (
    .DATA(data), .mem_slot(mem_slot), .clk(transistor_1_out), .result(out_6), .shutdown(comparator_2_eq));
  _16bitDispCntrl u_16bitdispcntrl_3 (
    .DATA(data), .mem_slot(mem_slot), .clk(transistor_1_out), .result(out_7), .shutdown(comparator_3_eq));
  _16bitDispCntrl u_16bitdispcntrl_4 (
    .DATA(data), .mem_slot(mem_slot), .clk(transistor_1_out), .result(out_8), .shutdown(comparator_4_eq));
  _16bitDispCntrl u_16bitdispcntrl_5 (
    .DATA(data), .mem_slot(mem_slot), .clk(transistor_1_out), .result(out_9), .shutdown(comparator_5_eq));
  _16bitDispCntrl u_16bitdispcntrl_6 (
    .DATA(data), .mem_slot(mem_slot), .clk(transistor_1_out), .result(out_10), .shutdown(comparator_6_eq));
  _16bitDispCntrl u_16bitdispcntrl_7 (
    .DATA(data), .mem_slot(mem_slot), .clk(transistor_1_out), .result(out_11), .shutdown(comparator_7_eq));
  _16bitDispCntrl u_16bitdispcntrl_8 (
    .DATA(data), .mem_slot(mem_slot), .clk(transistor_1_out), .result(out_12), .shutdown(comparator_8_eq));
  Comparator #(.width(4), .mode("unsigned")) comparator_9 (
    .a(mem_slot[7:4]), .b(4'b1000), .eq(comparator_9_eq));  // open: gt, lt
  Comparator #(.width(4), .mode("unsigned")) comparator_10 (
    .a(mem_slot[7:4]), .b(4'b1001), .eq(comparator_10_eq));  // open: gt, lt
  Comparator #(.width(4), .mode("unsigned")) comparator_11 (
    .a(mem_slot[7:4]), .b(4'b1010), .eq(comparator_11_eq));  // open: gt, lt
  Comparator #(.width(4), .mode("unsigned")) comparator_12 (
    .a(mem_slot[7:4]), .b(4'b1011), .eq(comparator_12_eq));  // open: gt, lt
  Comparator #(.width(4), .mode("unsigned")) comparator_13 (
    .a(mem_slot[7:4]), .b(4'b1100), .eq(comparator_13_eq));  // open: gt, lt
  Comparator #(.width(4), .mode("unsigned")) comparator_14 (
    .a(mem_slot[7:4]), .b(4'b1101), .eq(comparator_14_eq));  // open: gt, lt
  Comparator #(.width(4), .mode("unsigned")) comparator_15 (
    .a(mem_slot[7:4]), .b(4'b1110), .eq(comparator_15_eq));  // open: gt, lt
  Comparator #(.width(4), .mode("unsigned")) comparator_16 (
    .a(mem_slot[7:4]), .b(4'b1111), .eq(comparator_16_eq));  // open: gt, lt
  _16bitDispCntrl u_16bitdispcntrl_9 (
    .DATA(data), .mem_slot(mem_slot), .clk(transistor_1_out), .result(out_13), .shutdown(comparator_9_eq));
  _16bitDispCntrl u_16bitdispcntrl_10 (
    .DATA(data), .mem_slot(mem_slot), .clk(transistor_1_out), .result(out_14), .shutdown(comparator_10_eq));
  _16bitDispCntrl u_16bitdispcntrl_11 (
    .DATA(data), .mem_slot(mem_slot), .clk(transistor_1_out), .result(out_15), .shutdown(comparator_11_eq));
  _16bitDispCntrl u_16bitdispcntrl_12 (
    .DATA(data), .mem_slot(mem_slot), .clk(transistor_1_out), .result(out_16), .shutdown(comparator_12_eq));
  _16bitDispCntrl u_16bitdispcntrl_13 (
    .DATA(data), .mem_slot(mem_slot), .clk(transistor_1_out), .result(out_17), .shutdown(comparator_13_eq));
  _16bitDispCntrl u_16bitdispcntrl_14 (
    .DATA(data), .mem_slot(mem_slot), .clk(transistor_1_out), .result(out_18), .shutdown(comparator_14_eq));
  _16bitDispCntrl u_16bitdispcntrl_15 (
    .DATA(data), .mem_slot(mem_slot), .clk(transistor_1_out), .result(out_19), .shutdown(comparator_15_eq));
  _16bitDispCntrl u_16bitdispcntrl_16 (
    .DATA(data), .mem_slot(mem_slot), .clk(transistor_1_out), .result(out_20), .shutdown(comparator_16_eq));
endmodule
