// Logisim project workingReally.circ as structural Verilog: 1 circuit, main circuit main
module main (
  input  in_1,
  output out_2
);

  wire and_1_out, and_2_out, and_3_out, and_4_out, and_5_out, and_9_out, cdm_8_1_data_code_prime, CL, code,
       comparator_1_gt, comparator_2_lt, comparator_3_eq, comparator_4_eq, comparator_5_gt, comparator_6_lt,
       comparator_7_gt, comparator_8_eq, comparator_9_lt, comparator_10_gt, comparator_11_eq,
       comparator_12_lt, comparator_13_eq, comparator_14_eq, data, decoder_2_out0, decoder_3_out0,
       decoder_4_out0, displaydriver_1_collision, dispLd, dispSel, down, I_Osel, in_out, Iovspom, left, mem,
       nor_1_out, nor_2_out, not_1_out, not_2_out, not_3_out, not_4_out, not_5_out, not_6_out, not_7_out,
       not_8_out, not_9_out, or_1_out, or_2_out, RAM, right, transistor_1_out, up, \вторая_часть_адреса_out ,
       \Первая_часть_адреса_out ;
  wire [1:0] displaydriver_1_colliderrt;
  wire [2:0] page;
  wire [3:0] adder_1_out, adder_1_out_2;
  wire [6:0] controlled_buffer_1_out, register_1_q;
  wire [7:0] adr, cdm_8_1_data_out, cdm_8_1_r0, cdm_8_1_r1, cdm_8_1_r2, cdm_8_1_r3, cdm_8_1_sp,
       controlled_buffer_4_out, counter_1_q, dat, demultiplexer_1_out0, demultiplexer_1_out1,
       demultiplexer_2_out1, demultiplexer_3_out1, multiplexer_1_out, PC, register_2_q;
  wire [7:7] rs_latch_1_q_prime;
  wire [15:0] displaydriver_1_out_6, displaydriver_1_out_7, displaydriver_1_out_8, displaydriver_1_out_9,
       displaydriver_1_out_10, displaydriver_1_out_11, displaydriver_1_out_12, displaydriver_1_out_13,
       displaydriver_1_out_14, displaydriver_1_out_15, displaydriver_1_out_16, displaydriver_1_out_17,
       displaydriver_1_out_18, displaydriver_1_out_19, displaydriver_1_out_20, displaydriver_1_out_21;

  Clock clock_1 (.out(CL));
  assign controlled_buffer_1_out = left ? 7'b0000001 : 7'bz;  // Controlled_Buffer controlled_buffer_1
  // Probe on cdm_8_1_r0
  // Probe on cdm_8_1_r1
  Comparator comparator_1 (.a(PC), .b(8'h2), .gt(comparator_1_gt));  // open: eq, lt
  Comparator comparator_2 (.a(PC), .b(8'h13), .lt(comparator_2_lt));  // open: gt, eq
  Comparator #(.width(3)) comparator_3 (.a(3'b000), .b(page), .eq(comparator_3_eq));  // open: gt, lt
  Comparator #(.width(3)) comparator_4 (.a(page), .b(3'b000), .eq(comparator_4_eq));  // open: gt, lt
  Comparator comparator_5 (.a(PC), .b(8'hca), .gt(comparator_5_gt));  // open: eq, lt
  Comparator comparator_6 (.a(PC), .b(8'hd0), .lt(comparator_6_lt));  // open: gt, eq
  Comparator comparator_7 (.a(PC), .b(8'hd3), .gt(comparator_7_gt));  // open: eq, lt
  Comparator #(.width(3)) comparator_8 (.a(page), .b(3'b000), .eq(comparator_8_eq));  // open: gt, lt
  Comparator comparator_9 (.a(PC), .b(8'hd7), .lt(comparator_9_lt));  // open: gt, eq
  Transistor #(.\type ("n")) transistor_1 (.in(1'b0), .out(transistor_1_out), .gate(left));
  // Probe on PC
  // Probe on cdm_8_1_r3
  // Probe on cdm_8_1_r2
  Button button_1 ();  // open: out
  and and_1 (and_1_out, comparator_1_gt, comparator_2_lt, comparator_3_eq);
  and and_2 (and_2_out, comparator_4_eq, comparator_5_gt, comparator_6_lt);
  and and_3 (and_3_out, comparator_7_gt, comparator_8_eq, comparator_9_lt);
  Transistor #(.\type ("n")) transistor_2 (.in(1'b0), .out(transistor_1_out), .gate(right));
  assign controlled_buffer_1_out = right ? {7{1'b0}} : 7'bz;  // Controlled_Buffer controlled_buffer_2
  // Probe on cdm_8_1_sp
  or or_1 (or_1_out, and_3_out, and_1_out, and_2_out, and_4_out);
  assign controlled_buffer_1_out = up ? 7'b0000010 : 7'bz;  // Controlled_Buffer controlled_buffer_3
  not not_1 (not_1_out, transistor_1_out);
  not not_2 (not_2_out, Iovspom);
  Decoder #(.disabled(0)) decoder_1 (.out0(code), .out1(data), .sel(cdm_8_1_data_code_prime), .en(mem));
  CdM_8 cdm_8_1 (
    .data_code_prime(cdm_8_1_data_code_prime), .R0(cdm_8_1_r0), .R1(cdm_8_1_r1), .mem(mem), .R2(cdm_8_1_r2),
    .load_st_prime(in_out), .R3(cdm_8_1_r3), .addr(adr), .PC(PC), .SP(cdm_8_1_sp),
    .data_out(cdm_8_1_data_out), .data_in(controlled_buffer_4_out), .page(page), .clk(CL), .rset(out_2));  // open: PS, IAck, IRQ, vector, shadow
  assign controlled_buffer_4_out = in_out ? dat : 8'bz;  // Controlled_Buffer controlled_buffer_4
  Demultiplexer #(.width(8), .enable("false")) demultiplexer_1 (
    .out0(demultiplexer_1_out0), .out1(demultiplexer_1_out1), .in(adr), .sel(or_1_out));
  Decoder #(.disabled(0)) decoder_2 (.out0(decoder_2_out0), .out1(dispSel), .sel(or_1_out), .en(RAM));
  Comparator comparator_10 (.a(PC), .b(8'he3), .gt(comparator_10_gt));  // open: eq, lt
  Comparator #(.width(3)) comparator_11 (.a(page), .b(3'b000), .eq(comparator_11_eq));  // open: gt, lt
  and and_4 (and_4_out, comparator_10_gt, comparator_11_eq, comparator_12_lt);
  Comparator comparator_12 (.a(PC), .b(8'hf0), .lt(comparator_12_lt));  // open: gt, eq
  Transistor #(.\type ("n")) transistor_3 (.in(1'b0), .out(transistor_1_out), .gate(up));
  nor nor_1 (nor_1_out, transistor_1_out, not_1_out);
  nor nor_2 (nor_2_out, Iovspom, not_2_out);
  assign dat = not_3_out ? cdm_8_1_data_out : 8'bz;  // Controlled_Buffer controlled_buffer_5
  not not_3 (not_3_out, in_out);
  Transistor #(.\type ("n")) transistor_4 (.in(1'b0), .out(transistor_1_out), .gate(down));
  assign controlled_buffer_1_out = down ? 7'b0000011 : 7'bz;  // Controlled_Buffer controlled_buffer_6
  not not_4 (not_4_out, not_5_out);
  not not_5 (not_5_out, transistor_1_out);
  Pull_Resistor #(.pull(1)) pull_resistor_1 (.node(transistor_1_out));
  Register #(.width(7), .trigger("high")) register_1 (
    .D(controlled_buffer_1_out), .Q(register_1_q), .clk(not_4_out));  // open: en, clr
  RS_latch rs_latch_1 (.S(nor_1_out), .R(nor_2_out), .Q_prime(rs_latch_1_q_prime[7]));  // open: Q, reset
  RAM ram_1 (.addr(demultiplexer_1_out1), .data(dat), .sel(dispSel), .clk(CL), .ld(dispLd));  // open: clr
  assign dat = Iovspom ? {rs_latch_1_q_prime[7], register_1_q} : 8'bz;  // Controlled_Buffer controlled_buffer_7
  ROM rom_1 (.addr(adr), .data(dat), .sel(code));
  RAM ram_2 (
    .addr(demultiplexer_1_out0), .data(dat), .sel(decoder_2_out0), .clk(CL), .ld(decoder_3_out0));  // open: clr
  Decoder #(.disabled(0)) decoder_3 (.out0(decoder_3_out0), .out1(dispLd), .sel(or_1_out), .en(in_out));
  Register register_2 (.D(dat), .Q(register_2_q), .clk(decoder_4_out0));  // open: en, clr
  not not_6 (not_6_out, Iovspom);
  Hex_Digit_Display hex_digit_display_1 (.value(register_2_q[7:4]));  // open: dp
  // Probe on demultiplexer_2_out1
  Demultiplexer #(.width(8), .enable("false")) demultiplexer_2 (
    .out1(demultiplexer_2_out1), .in(dat), .sel(or_2_out));  // open: out0
  not not_7 (not_7_out, RAM);
  and and_5 (and_5_out, not_7_out, not_6_out, data);
  Button button_2 (.out(up));
  Button button_3 (.out(left));
  Button button_4 (.out(right));
  Button button_5 (.out(down));
  and \u_вторая_часть_адреса  (\вторая_часть_адреса_out , I_Osel, adr[0], adr[1], ~adr[2], ~adr[3]);  // AND_Gate
  Decoder #(.disabled(0)) decoder_4 (
    .out0(decoder_4_out0), .out1(Iovspom), .sel(in_out), .en(\вторая_часть_адреса_out ));
  Hex_Digit_Display hex_digit_display_2 (.value(register_2_q[3:0]));  // open: dp
  Demultiplexer #(.width(8), .enable("false")) demultiplexer_3 (
    .out1(demultiplexer_3_out1), .in(adr), .sel(or_2_out));  // open: out0
  or or_2 (or_2_out, dispSel, and_5_out);
  // Probe on demultiplexer_3_out1
  and and_6 (I_Osel, not_9_out, CL, data);
  Comparator #(.width(2)) comparator_13 (
    .a(2'b01), .b(displaydriver_1_colliderrt), .eq(comparator_13_eq));  // open: gt, lt
  displayDriver displaydriver_1 (
    .data(demultiplexer_2_out1), .mem_slot(demultiplexer_3_out1), .out_6(displaydriver_1_out_6),
    .out_7(displaydriver_1_out_7), .out_8(displaydriver_1_out_8), .out_9(displaydriver_1_out_9),
    .out_10(displaydriver_1_out_10), .out_11(displaydriver_1_out_11), .out_12(displaydriver_1_out_12),
    .out_13(displaydriver_1_out_13), .out_14(displaydriver_1_out_14), .out_15(displaydriver_1_out_15),
    .out_16(displaydriver_1_out_16), .out_17(displaydriver_1_out_17), .out_18(displaydriver_1_out_18),
    .out_19(displaydriver_1_out_19), .out_20(displaydriver_1_out_20), .out_21(displaydriver_1_out_21),
    .CLK(CL), .shutdown(not_8_out), .RESET(out_2), .collision(displaydriver_1_collision),
    .colliderRT(displaydriver_1_colliderrt));  // open: colliderSaved
  DotMatrix #(.inputtype("row"), .matrixcols(16), .matrixrows(16)) dotmatrix_1 (
    .row0(displaydriver_1_out_6), .row1(displaydriver_1_out_7), .row2(displaydriver_1_out_8),
    .row3(displaydriver_1_out_9), .row4(displaydriver_1_out_10), .row5(displaydriver_1_out_11),
    .row6(displaydriver_1_out_12), .row7(displaydriver_1_out_13), .row8(displaydriver_1_out_14),
    .row9(displaydriver_1_out_15), .row10(displaydriver_1_out_16), .row11(displaydriver_1_out_17),
    .row12(displaydriver_1_out_18), .row13(displaydriver_1_out_19), .row14(displaydriver_1_out_20),
    .row15(displaydriver_1_out_21));
  not not_8 (not_8_out, or_2_out);
  not not_9 (not_9_out, \Первая_часть_адреса_out );
  and and_7 (RAM, \Первая_часть_адреса_out , data);
  and and_8 (out_2, comparator_13_eq, displaydriver_1_collision);
  nand \u_Первая_часть_адреса  (\Первая_часть_адреса_out , ~adr[4], adr[5], adr[6], adr[7]);  // NAND_Gate
  Comparator #(.width(2)) comparator_14 (
    .a(2'b11), .b(displaydriver_1_colliderrt), .eq(comparator_14_eq));  // open: gt, lt
  Hex_Digit_Display hex_digit_display_3 (.value(adder_1_out));  // open: dp
  Hex_Digit_Display hex_digit_display_4 (.value(adder_1_out_2));  // open: dp
  Multiplexer #(.width(8)) multiplexer_1 (
    .in0({adder_1_out_2, adder_1_out}), .in1({8{1'b0}}), .out(multiplexer_1_out), .sel(in_1));  // open: en
  Counter counter_1 (.D(multiplexer_1_out), .Q(counter_1_q), .clk(and_9_out), .clr(out_2));  // open: load, count, carry
  and and_9 (and_9_out, displaydriver_1_collision, comparator_14_eq);
  Adder adder_1 (.a({8{1'b0}}), .b(counter_1_q), .out({adder_1_out_2, adder_1_out}));  // open: cin, cout
  Pull_Resistor pull_resistor_2 (.node(adr[0]));
  Pull_Resistor pull_resistor_3 (.node(adr[1]));
  Pull_Resistor pull_resistor_4 (.node(adr[2]));
  Pull_Resistor pull_resistor_5 (.node(adr[3]));
  Pull_Resistor pull_resistor_6 (.node(adr[4]));
  Pull_Resistor pull_resistor_7 (.node(adr[5]));
  Pull_Resistor pull_resistor_8 (.node(adr[6]));
  Pull_Resistor pull_resistor_9 (.node(adr[7]));

  // Other names for the same wires on the sheet: I_Oadr[3:0] = adr[3:0]; I_Odat[7:0] = dat; rd_wr = in_out;
  //   RESET = out_2

  // Notes on the sheet:
  //   contents of rom_1 (hex, n*v repeats v):
  //   cd ff a f d0 3 d1 b1 a4 d0 1 d1 f0 a4 8d a4 8d a4 f a d0 a0 a1 8c d1 f0 a1 8c d1 b2 a1 8c d1 b0 a1
  //   d0 90 d1 b1 a1 35 c1 c5 5 e1 37 d0 a0 b2 8e a2 d6 c7 ee 63 d0 1 74 e1 45 d0 a0 b2 8a a2 d6 c7 ee 63
  //   d0 2 74 e1 55 d0 a0 b2 d3 10 3b a3 d6 c7 ee 63 d0 3 74 e1 63 d0 a0 b2 d3 10 1e a2 d6 c7 d0 a2 b0 a1
  //   c1 d1 a2 d6 d9 d0 a0 b0 d1 90 b5 74 e1 7c d6 e3 d0 90 a1 ee bd d0 a3 b0 b0 0 e1 8c d1 a1 b6 d6 d2 8e
  //   a6 ee b8 d1 1 71 e1 9a d1 a1 b6 d6 d2 8a a6 ee b8 d1 2 71 e1 aa d1 a1 b6 d6 d2 d3 10 3b a7 ee b8 d1
  //   3 71 e1 b8 d1 a1 b6 d6 d2 d3 10 1b a7 d1 a3 b4 d6 d9 d0 e3 b0 0 e4 2a c5 c0 ee 2a d0 a0 b0 a f d2 1
  //   a2 f a d7 30 f f a8 f f d7 d2 bf 8c 72 ed e1 d0 b0 a4 d7 9d 8d 9d b4 0 e0 ec ee e3 d0 3 a4 a a d7 d4
endmodule
