// Logisim project workingReally_1.circ as structural Verilog: 4 circuits, main circuit main
module main (
);

  wire cdm_8_1_data_code_prime, CL, code, data, decoder_2_out0, displaydriver_1_collision, dispSel, down,
       I_Osel, in_out, Iovspom, left, mem, memeryswitcher_1_datald, memeryswitcher_1_datasel,
       memeryswitcher_1_displld, nor_1_out, nor_2_out, not_1_out, not_2_out, not_3_out, not_4_out, not_5_out,
       not_6_out, RAM, RESET, right, rowdisplcontroller_1_on_off, transistor_1_out, up,
       \вторая_часть_адреса_out , \Первая_часть_адреса_out ;
  wire [1:0] displaydriver_1_colliderrt;
  wire [2:0] page;
  wire [3:0] exitandnumcheck_1_firstnum, exitandnumcheck_1_secondnum;
  wire [6:0] controlled_buffer_1_out, register_1_q;
  wire [7:0] adr, cdm_8_1_data_out, cdm_8_1_r0, cdm_8_1_r1, cdm_8_1_r2, cdm_8_1_r3, cdm_8_1_sp,
       controlled_buffer_3_out, dat, memeryswitcher_1_dataaddr, memeryswitcher_1_displaddr, PC, register_2_q,
       rowdisplcontroller_1_data_2, rowdisplcontroller_1_mem_slot;
  wire [7:7] rs_latch_1_q_prime;
  wire [15:0] displaydriver_1_out_6, displaydriver_1_out_7, displaydriver_1_out_8, displaydriver_1_out_9,
       displaydriver_1_out_10, displaydriver_1_out_11, displaydriver_1_out_12, displaydriver_1_out_13,
       displaydriver_1_out_14, displaydriver_1_out_15, displaydriver_1_out_16, displaydriver_1_out_17,
       displaydriver_1_out_18, displaydriver_1_out_19, displaydriver_1_out_20, displaydriver_1_out_21;

  Clock clock_1 (.out(CL));
  // Probe on cdm_8_1_r1
  // Probe on cdm_8_1_r0
  Transistor #(.\type ("n")) transistor_1 (.in(1'b0), .out(transistor_1_out), .gate(left));
  assign controlled_buffer_1_out = left ? 7'b0000001 : 7'bz;  // Controlled_Buffer controlled_buffer_1
  // Probe on PC
  // Probe on cdm_8_1_r3
  // Probe on cdm_8_1_r2
  assign controlled_buffer_1_out = right ? {7{1'b0}} : 7'bz;  // Controlled_Buffer controlled_buffer_2
  // Probe on cdm_8_1_sp
  Transistor #(.\type ("n")) transistor_2 (.in(1'b0), .out(transistor_1_out), .gate(right));
  not not_1 (not_1_out, transistor_1_out);
  Decoder #(.disabled(0)) decoder_1 (.out0(code), .out1(data), .sel(cdm_8_1_data_code_prime), .en(mem));
  CdM_8 cdm_8_1 (
    .data_code_prime(cdm_8_1_data_code_prime), .R0(cdm_8_1_r0), .R1(cdm_8_1_r1), .mem(mem), .R2(cdm_8_1_r2),
    .load_st_prime(in_out), .R3(cdm_8_1_r3), .addr(adr), .PC(PC), .SP(cdm_8_1_sp),
    .data_out(cdm_8_1_data_out), .data_in(controlled_buffer_3_out), .page(page), .clk(CL), .rset(RESET));  // open: PS, IAck, IRQ, vector, shadow
  assign controlled_buffer_3_out = in_out ? dat : 8'bz;  // Controlled_Buffer controlled_buffer_3
  memerySwitcher memeryswitcher_1 (
    .Addr(adr), .PC(PC), .RAM(RAM), .page(page), .rd_wr(in_out), .dataAddr(memeryswitcher_1_dataaddr),
    .displAddr(memeryswitcher_1_displaddr), .dataSel(memeryswitcher_1_datasel), .displSel(dispSel),
    .dataLd(memeryswitcher_1_datald), .displLd(memeryswitcher_1_displld));
  Transistor #(.\type ("n")) transistor_3 (.in(1'b0), .out(transistor_1_out), .gate(up));
  assign controlled_buffer_1_out = up ? 7'b0000010 : 7'bz;  // Controlled_Buffer controlled_buffer_4
  nor nor_1 (nor_1_out, transistor_1_out, not_1_out);
  nor nor_2 (nor_2_out, Iovspom, not_2_out);
  not not_2 (not_2_out, Iovspom);
  assign dat = not_3_out ? cdm_8_1_data_out : 8'bz;  // Controlled_Buffer controlled_buffer_5
  not not_3 (not_3_out, in_out);
  Transistor #(.\type ("n")) transistor_4 (.in(1'b0), .out(transistor_1_out), .gate(down));
  assign controlled_buffer_1_out = down ? 7'b0000011 : 7'bz;  // Controlled_Buffer controlled_buffer_6
  not not_4 (not_4_out, transistor_1_out);
  Pull_Resistor #(.pull(1)) pull_resistor_1 (.node(transistor_1_out));
  Register #(.width(7), .trigger("high")) register_1 (
    .D(controlled_buffer_1_out), .Q(register_1_q), .clk(not_5_out));  // open: en, clr
  RS_latch rs_latch_1 (.S(nor_1_out), .R(nor_2_out), .Q_prime(rs_latch_1_q_prime[7]));  // open: Q, reset
  RAM ram_1 (
    .addr(memeryswitcher_1_dataaddr), .data(dat), .sel(memeryswitcher_1_datasel), .clk(CL),
    .ld(memeryswitcher_1_datald));  // open: clr
  RAM ram_2 (
    .addr(memeryswitcher_1_displaddr), .data(dat), .sel(dispSel), .clk(CL), .ld(memeryswitcher_1_displld));  // open: clr
  not not_5 (not_5_out, not_4_out);
  ROM rom_1 (.addr(adr), .data(dat), .sel(code));
  assign dat = Iovspom ? {rs_latch_1_q_prime[7], register_1_q} : 8'bz;  // Controlled_Buffer controlled_buffer_7
  Hex_Digit_Display hex_digit_display_1 (.value(register_2_q[7:4]));  // open: dp
  Register register_2 (.D(dat), .Q(register_2_q), .clk(decoder_2_out0));  // open: en, clr
  and \u_вторая_часть_адреса  (\вторая_часть_адреса_out , I_Osel, adr[0], adr[1], ~adr[2], ~adr[3]);  // AND_Gate
  Hex_Digit_Display hex_digit_display_2 (.value(register_2_q[3:0]));  // open: dp
  Decoder #(.disabled(0)) decoder_2 (
    .out0(decoder_2_out0), .out1(Iovspom), .sel(in_out), .en(\вторая_часть_адреса_out ));
  rowDisplController rowdisplcontroller_1 (
    .data(dat), .Addr(adr), .displSel(dispSel), .RAM(RAM), .dataSel(data), .isIO(Iovspom),
    .data_2(rowdisplcontroller_1_data_2), .mem_slot(rowdisplcontroller_1_mem_slot),
    .on_off(rowdisplcontroller_1_on_off));
  displayDriver displaydriver_1 (
    .data(rowdisplcontroller_1_data_2), .mem_slot(rowdisplcontroller_1_mem_slot),
    .out_6(displaydriver_1_out_6), .out_7(displaydriver_1_out_7), .out_8(displaydriver_1_out_8),
    .out_9(displaydriver_1_out_9), .out_10(displaydriver_1_out_10), .out_11(displaydriver_1_out_11),
    .out_12(displaydriver_1_out_12), .out_13(displaydriver_1_out_13), .out_14(displaydriver_1_out_14),
    .out_15(displaydriver_1_out_15), .out_16(displaydriver_1_out_16), .out_17(displaydriver_1_out_17),
    .out_18(displaydriver_1_out_18), .out_19(displaydriver_1_out_19), .out_20(displaydriver_1_out_20),
    .out_21(displaydriver_1_out_21), .CLK(CL), .shutdown(rowdisplcontroller_1_on_off), .RESET(RESET),
    .collision(displaydriver_1_collision), .colliderRT(displaydriver_1_colliderrt));  // open: colliderSaved
  not not_6 (not_6_out, \Первая_часть_адреса_out );
  and and_1 (I_Osel, not_6_out, CL, data);
  Hex_Digit_Display hex_digit_display_3 (.value(exitandnumcheck_1_firstnum));  // open: dp
  Hex_Digit_Display hex_digit_display_4 (.value(exitandnumcheck_1_secondnum));  // open: dp
  ExitAndNumCheck exitandnumcheck_1 (
    .Collision(displaydriver_1_collision), .Collider(displaydriver_1_colliderrt), .Reset(RESET),
    .firstNum(exitandnumcheck_1_firstnum), .secondNum(exitandnumcheck_1_secondnum));
  DotMatrix #(.inputtype("row"), .matrixcols(16), .matrixrows(16)) dotmatrix_1 (
    .row0(displaydriver_1_out_6), .row1(displaydriver_1_out_7), .row2(displaydriver_1_out_8),
    .row3(displaydriver_1_out_9), .row4(displaydriver_1_out_10), .row5(displaydriver_1_out_11),
    .row6(displaydriver_1_out_12), .row7(displaydriver_1_out_13), .row8(displaydriver_1_out_14),
    .row9(displaydriver_1_out_15), .row10(displaydriver_1_out_16), .row11(displaydriver_1_out_17),
    .row12(displaydriver_1_out_18), .row13(displaydriver_1_out_19), .row14(displaydriver_1_out_20),
    .row15(displaydriver_1_out_21));
  and and_2 (RAM, \Первая_часть_адреса_out , data);
  nand \u_Первая_часть_адреса  (\Первая_часть_адреса_out , ~adr[4], adr[5], adr[6], adr[7]);  // NAND_Gate
  Button button_1 (.out(left));
  Button button_2 (.out(up));
  Button button_3 (.out(right));
  Button button_4 (.out(down));
  Pull_Resistor pull_resistor_2 (.node(adr[0]));
  Pull_Resistor pull_resistor_3 (.node(adr[1]));
  Pull_Resistor pull_resistor_4 (.node(adr[2]));
  Pull_Resistor pull_resistor_5 (.node(adr[3]));
  Pull_Resistor pull_resistor_6 (.node(adr[4]));
  Pull_Resistor pull_resistor_7 (.node(adr[5]));
  Pull_Resistor pull_resistor_8 (.node(adr[6]));
  Pull_Resistor pull_resistor_9 (.node(adr[7]));

  // Other names for the same wires on the sheet: I_Oadr[3:0] = adr[3:0]; I_Odat[7:0] = dat; rd_wr = in_out

  // Notes on the sheet:
  //   contents of rom_1 (hex, n*v repeats v):
  //   cd ff a f d0 3 d1 b1 a4 d0 1 d1 f0 a4 8d a4 8d a4 f a d0 a0 a1 8c d1 f0 a1 8c d1 b2 a1 8c d1 b0 a1
  //   d0 90 d1 b1 a1 35 c1 c5 5 e1 37 d0 a0 b2 8e a2 d6 c7 ee 63 d0 1 74 e1 45 d0 a0 b2 8a a2 d6 c7 ee 63
  //   d0 2 74 e1 55 d0 a0 b2 d3 10 3b a3 d6 c7 ee 63 d0 3 74 e1 63 d0 a0 b2 d3 10 1e a2 d6 c7 d0 a2 b0 a1
  //   c1 d1 a2 d6 d9 d0 a0 b0 d1 90 b5 74 e1 7c d6 e3 d0 90 a1 ee bd d0 a3 b0 b0 0 e1 8c d1 a1 b6 d6 d2 8e
  //   a6 ee b8 d1 1 71 e1 9a d1 a1 b6 d6 d2 8a a6 ee b8 d1 2 71 e1 aa d1 a1 b6 d6 d2 d3 10 3b a7 ee b8 d1
  //   3 71 e1 b8 d1 a1 b6 d6 d2 d3 10 1b a7 d1 a3 b4 d6 d9 d0 e3 b0 0 e4 2a c5 c0 ee 2a d0 a0 b0 a f d2 1
  //   a2 f a d7 30 f f a8 f f d7 d2 bf 8c 72 ed e1 d0 b0 a4 d7 9d 8d 9d b4 0 e0 ec ee e3 d0 3 a4 a a d7 d4
endmodule

module memerySwitcher (
  input  [7:0] Addr,
  input  [7:0] PC,
  input  RAM,
  input  [2:0] page,
  input  rd_wr,
  output [7:0] dataAddr,
  output [7:0] displAddr,
  output dataSel,
  output displSel,
  output dataLd,
  output displLd
);

  wire and_1_out, and_2_out, and_3_out, and_4_out, and_5_out, comparator_1_gt, comparator_2_lt,
       comparator_3_gt, comparator_4_lt, comparator_5_gt, comparator_6_lt, comparator_7_gt, comparator_8_lt,
       comparator_9_eq, or_1_out;

  Comparator comparator_1 (.a(PC), .b(8'h2), .gt(comparator_1_gt));  // open: eq, lt
  Comparator comparator_2 (.a(PC), .b(8'h13), .lt(comparator_2_lt));  // open: gt, eq
  Comparator comparator_3 (.a(PC), .b(8'hca), .gt(comparator_3_gt));  // open: eq, lt
  Comparator comparator_4 (.a(PC), .b(8'hd0), .lt(comparator_4_lt));  // open: gt, eq
  Comparator comparator_5 (.a(PC), .b(8'hd3), .gt(comparator_5_gt));  // open: eq, lt
  Comparator comparator_6 (.a(PC), .b(8'hd7), .lt(comparator_6_lt));  // open: gt, eq
  Comparator comparator_7 (.a(PC), .b(8'he3), .gt(comparator_7_gt));  // open: eq, lt
  Comparator comparator_8 (.a(PC), .b(8'hf0), .lt(comparator_8_lt));  // open: gt, eq
  and and_1 (and_1_out, comparator_1_gt, comparator_2_lt);
  and and_2 (and_2_out, comparator_3_gt, comparator_4_lt);
  and and_3 (and_3_out, comparator_5_gt, comparator_6_lt);
  and and_4 (and_4_out, comparator_7_gt, comparator_8_lt);
  or or_1 (or_1_out, and_1_out, and_2_out, and_3_out, and_4_out);
  Comparator #(.width(3)) comparator_9 (.a(3'b000), .b(page), .eq(comparator_9_eq));  // open: gt, lt
  Demultiplexer #(.width(8), .enable("false")) demultiplexer_1 (
    .out0(dataAddr), .out1(displAddr), .in(Addr), .sel(and_5_out));
  and and_5 (and_5_out, or_1_out, comparator_9_eq);
  Decoder #(.disabled(0)) decoder_1 (.out0(dataSel), .out1(displSel), .sel(and_5_out), .en(RAM));
  Decoder #(.disabled(0)) decoder_2 (.out0(dataLd), .out1(displLd), .sel(and_5_out), .en(rd_wr));
endmodule

module rowDisplController (
  input  [7:0] data,
  input  [7:0] Addr,
  input  displSel,
  input  RAM,
  input  dataSel,
  input  isIO,
  output [7:0] data_2,
  output [7:0] mem_slot,
  output on_off
);

  wire and_1_out, not_1_out, not_2_out, or_1_out;

  not not_1 (not_1_out, RAM);
  not not_2 (not_2_out, isIO);
  and and_1 (and_1_out, not_1_out, not_2_out, dataSel);
  Demultiplexer #(.width(8), .enable("false")) demultiplexer_1 (
    .out1(data_2), .in(data), .sel(or_1_out));  // open: out0
  Demultiplexer #(.width(8), .enable("false")) demultiplexer_2 (
    .out1(mem_slot), .in(Addr), .sel(or_1_out));  // open: out0
  or or_1 (or_1_out, displSel, and_1_out);
  not not_3 (on_off, or_1_out);
endmodule

module ExitAndNumCheck (
  input  Collision,
  input  [1:0] Collider,
  output [3:0] firstNum,
  output [3:0] secondNum,
  output Reset
);

  wire and_2_out, comparator_1_eq, comparator_2_eq;
  wire [7:0] counter_1_q;

  Comparator #(.width(2)) comparator_1 (.a(2'b01), .b(Collider), .eq(comparator_1_eq));  // open: gt, lt
  and and_1 (Reset, comparator_1_eq, Collision);
  Comparator #(.width(2)) comparator_2 (.a(2'b11), .b(Collider), .eq(comparator_2_eq));  // open: gt, lt
  Counter counter_1 (
    .D({secondNum, firstNum}), .Q(counter_1_q), .clk(and_2_out), .clr(Reset));  // open: load, count, carry
  and and_2 (and_2_out, Collision, comparator_2_eq);
  Adder adder_1 (.a({8{1'b0}}), .b(counter_1_q), .out({secondNum, firstNum}));  // open: cin, cout
endmodule
